# Fritzing sketch CarDriverCircuit (saved by Fritzing 0.9.2b)
breadboards: 1

parts:
  Part1 = Bluetooth HC-06
  Part2 = Arduino Uno (Rev3) - ICSP
  IC1 = L293D [package=THT]
  M1 = DC Motor
  M2 = DC Motor
  VCC1 = Battery block 9V

nets:
  N1: Part1.RXD, Part2.D1/TX
  N2: Part1.TXD, Part2.D0/RX
  GND: Part1.GND, Part2.GND, IC1.0V, VCC1.-
  VCC: Part1.VCC, Part2.5V, IC1.+V
  N3: Part2.D9_PWM, IC1.Enable_1, IC1.Enable_2
  N4: Part2.D10_PWM/SS, IC1.In_1
  N5: Part2.D11_PWM/MOSI, IC1.In_2
  N6: Part2.D12/MISO, IC1.In_4
  N7: Part2.D13/SCK, IC1.In_3
  N8: IC1.Out_1_(_Controlled_by_Enable_1_), M1.pin_2
  N9: IC1.Out_2_(_Controlled_by_Enable_1_), M1.pin_1
  N10: IC1.+Vmotor, VCC1.+
  N11: IC1.Out_3_(_Controlled_by_Enable_2_), M2.pin_2
  N12: IC1.Out_4_(_Controlled_by_Enable_2_), M2.pin_1
